# Fritzing sketch Wire_Diagram (saved by Fritzing 0.9.3b)
circuit board: 8.46667cm x 5.64444cm

parts:
  Raspberry_Pi_Zero1 = Raspberry Pi Zero
  Part1 = Arduino Pro Mini (5V)
  hc-sr1 = hc-sr04
  Q1 = MOSFET-NCHANNEL [package=to220v]

nets:
  N1: Raspberry_Pi_Zero1.GPIO3, Part1.D7
  N2: Raspberry_Pi_Zero1.GPIO17, Part1.D8
  N3: Raspberry_Pi_Zero1.GPIO27, Part1.SCK
  GND: Raspberry_Pi_Zero1.GND, Part1.GND, hc-sr1.GND
  N4: Part1.VCC, Q1.G
  N5: Part1.MISO, hc-sr1.Trig
  N6: Part1.MOSI, hc-sr1.Echo
  N7: Part1.D9, Q1.D
  N8: hc-sr1.VCC, Q1.S
